# Fritzing sketch DIYSwitch (saved by Fritzing 0.9.4)
breadboards: 1

parts:
  Part1 = Arduino Leonardo (Rev3b)
  J1 = Piezo Speaker
  LED1 = smd LED [color="Red (633nm)" package="0603 [SMD]"]
  R2 = Resistor [tolerance=±5% resistance=220 package="0805 [SMD]"]

nets:
  N1: Part1.D5_PWM, J1.pin2
  N2: Part1.GND, J1.pin1, LED1.cathode
  N3: Part1.D9_PWM/A9, R2.Pin_0
  N4: LED1.anode, R2.Pin_1

notes:
  Switch side A
  You can use either the LED or the buzzer as an output. Both circuits are displayed here for convenience!
  Switch side B
